# Fritzing sketch RASPBERRY_m (saved by Fritzing 0.9.3b)
breadboards: 1

parts:
  Raspberry_Pi_1 = Raspberry Pi 3 [part_number=RPI-3-V1.2]
  TELEGRAM = Square Pushbutton
  REGISTRA = Square Pushbutton
  CANCELLA = Square Pushbutton
  TELEGRAM_2 = LEDs [package=led10mm]
  SP_OK = LEDs [package=led10mm]
  SP_ERROR = LEDs [package=led10mm]
  R1 = Resistor [tolerance=±5% resistance=330 package="0603 [SMD]"]
  R2 = Resistor [tolerance=±5% resistance=330 package="0603 [SMD]"]
  R3 = Resistor [tolerance=±5% resistance=330 package="0603 [SMD]"]
  DISPLAY_1-SDA_0-SCK = Grove OLED 128x96

nets:
  3V3: Raspberry_Pi_1.3v3, Raspberry_Pi_1.3V3, DISPLAY_1-SDA_0-SCK.VCC
  N1: Raspberry_Pi_1.GPIO2, DISPLAY_1-SDA_0-SCK.SDA
  N2: Raspberry_Pi_1.GPIO3, DISPLAY_1-SDA_0-SCK.SCL
  N3: Raspberry_Pi_1.GIPO17, REGISTRA.leg1
  N4: Raspberry_Pi_1.GIPO27, CANCELLA.leg1
  N5: Raspberry_Pi_1.GIPO22, TELEGRAM.leg1
  GND: Raspberry_Pi_1.GND, TELEGRAM.leg0, REGISTRA.leg0, CANCELLA.leg0, R1.Pin_1, R2.Pin_1, R3.Pin_1, DISPLAY_1-SDA_0-SCK.GND
  N6: Raspberry_Pi_1.GIPO25, SP_ERROR.A
  N7: Raspberry_Pi_1.GIPO24, SP_OK.A
  N8: Raspberry_Pi_1.GIPO23, TELEGRAM_2.A
  N9: TELEGRAM_2.C, R3.Pin_0
  N10: SP_OK.C, R2.Pin_0
  N11: SP_ERROR.C, R1.Pin_0
